// Logisim project Lab_1.circ as structural Verilog: 4 circuits, main circuit 2:1 MUX
module _2_1_MUX (
  input  A,
  input  S,
  input  B,
  output out_4
);

  wire and_1_out, and_2_out, not_1_out;

  not not_1 (not_1_out, S);
  and and_1 (and_1_out, A, not_1_out);
  and and_2 (and_2_out, S, B);
  or or_1 (out_4, and_1_out, and_2_out);

  // Notes on the sheet:
  //   2:1 Multiplexer: NOT, AND and OR gates
endmodule

module _4_1_MUX (
  input  A,
  input  B,
  input  S1,
  input  S0,
  input  C,
  input  D,
  output out_7
);

  wire n2_1_mux_1_out_4, n2_1_mux_2_out_4;

  _2_1_MUX u_2_1_mux_1 (.A(A), .S(S0), .B(B), .out_4(n2_1_mux_1_out_4));
  _2_1_MUX u_2_1_mux_2 (.A(C), .S(S0), .B(D), .out_4(n2_1_mux_2_out_4));
  _2_1_MUX u_2_1_mux_3 (.A(n2_1_mux_1_out_4), .S(S1), .B(n2_1_mux_2_out_4), .out_4(out_7));

  // Notes on the sheet:
  //   4:1 Multiplexer from 2:1 MUX
endmodule

module _8_1_MUX (
  input  S0,
  input  S1,
  input  A,
  input  B,
  input  C,
  input  S4,
  input  D,
  input  E,
  input  F,
  input  G,
  input  H,
  input  S2,
  input  S3,
  output out_14
);

  wire n4_1_mux_1_out_7, n4_1_mux_2_out_7;

  _4_1_MUX u_4_1_mux_1 (.A(A), .B(B), .S1(S1), .S0(S0), .C(C), .D(D), .out_7(n4_1_mux_1_out_7));
  _4_1_MUX u_4_1_mux_2 (.A(E), .B(F), .S1(S3), .S0(S2), .C(G), .D(H), .out_7(n4_1_mux_2_out_7));
  _2_1_MUX u_2_1_mux_1 (.A(n4_1_mux_1_out_7), .S(S4), .B(n4_1_mux_2_out_7), .out_4(out_14));

  // Notes on the sheet:
  //   8:1 Multiplexer
endmodule

module _2_1_MUX_NAND (
  input  A,
  input  S,
  input  B,
  output out_4
);

  wire nand_1_out, nand_2_out, nand_3_out;

  nand nand_1 (nand_1_out, 1'b1, S);
  nand nand_2 (nand_2_out, A, nand_1_out);
  nand nand_3 (nand_3_out, S, B);
  nand nand_4 (out_4, nand_2_out, nand_3_out);

  // Notes on the sheet:
  //   2:1 Multiplexer: NAND gates
endmodule
